# Fritzing sketch meteo_fritzing_sketch (saved by Fritzing 0.9.3b)
breadboards: 1

parts:
  U1 = ESP8266 WiFi Module [part_number=ESP8266]
  U2 = Mini-360 DC-DC Buck converter [package=THT]
  D1 = Rectifier Diode [part_number=1N4001 package="300 mil [THT]"]
  TP1 = TP4056 [chip_label=TP4056 package="DIP (Dual Inline) [THT]"]
  BAT1 = Battery Holders [package=battery-aa]
  DS1 = DS18B20 1-Wire Temperature Sensor [part_number=DS18B20]
  LED1 = LED - 5mm [color="Red (633nm)" package="5 mm [THT]"]
  J1 = male pin header, 1 pin [form="♂ (male)"]
  Part1 = BMP180 Breakout (GY-68)
  R3 = Resistor [tolerance=±5% resistance=500 package="0805 [SMD]"]
  R2 = Resistor [tolerance=±5% resistance=10k package="0805 [SMD]"]
  R1 = Resistor [tolerance=±5% resistance=10k package="0805 [SMD]"]
  A = male pin header, 1 pin [form="♂ (male)"]
  J5 = male pin header, 1 pin [form="♂ (male)"]
  J6 = male pin header, 1 pin [form="♂ (male)"]
  Q1 = MOSFET-NCHANNEL [package=sot23-3]
  Part3 = Si7021
  Part2 = BH1750
  R4 = Resistor [tolerance=±5% resistance=10k package="0805 [SMD]"]
  R5 = Resistor [tolerance=±5% resistance=10k package="0805 [SMD]"]
  R6 = Resistor [tolerance=±5% resistance=10k package="0805 [SMD]"]

nets:
  N1: U1.IO0, J1.pin1
  N2: U1.IO4, R1.Pin_0
  N3: U1.3.3V#10, J6.pin1
  N4: U1.GND#12, U2.OUT-, R2.Pin_1, Q1.S, R6.Pin_0
  N5: U1.GND#13, R3.Pin_0, J5.pin1
  N6: U1.IO5, LED1.anode
  N7: U1.T_OUT, A.pin1
  N8: U1.RST, R4.Pin_0
  N9: U1.CHIP_EN, R5.Pin_1
  N10: U1.XPD, R4.Pin_1
  N11: U1.IO14, Part1.SDA, Part3.SDA, Part2.SDA
  N12: U1.IO12, Part1.SCL, Part3.SCL, Part2.SCL
  N13: U1.IO13, DS1.DQ
  N14: U1.IO15, R6.Pin_1
  N15: U2.IN-, TP1.pin6
  N16: U2.IN+, D1.cathode
  VCC: U2.OUT+, DS1.VDD, Part1.VCC, Part3.VCC, Part2.VCC, R5.Pin_0
  N17: D1.anode, TP1.pin3
  N18: TP1.pin4, BAT1.+
  N19: TP1.pin5, BAT1.-
  GND: DS1.GND, Part1.GND, Q1.D, Part3.GND, Part2.GND
  N20: LED1.cathode, R3.Pin_1
  N21: R2.Pin_0, R1.Pin_1, Q1.G

notes:
  2n7002 sot23

custom parts:
  Mini-360 DC-DC Buck converter: Mini-360 DC-DC Buck converter. Tiny buck step down voltage converter, input voltage 4.75 to 23V output 1 to 17V adjustable. Available from ebay and the like.
  TP4056: A DIP stand-in part for whatever IC you want. With 6 pins on a 300mil dual inline package (DIP) footprint.
  Battery Holders: Battery Holders Various common sizes : AA, AAA, 20mm coin cell and 12mm coin cell.
  BMP180 Breakout (GY-68): This is a simple breakout board for the BMP180, a high-precision, low-power barometric pressure sensor made by Bosch Sensortec. The range of measurement is from 300hPa to 1100hPa. The sensor can be supplied with voltage ranging from 1.8V to 3.6V. Operating temperature range is -40 to +85 °C. This particular breakout board (or perhaps the configuration) is produced by Shenzhen Keep Power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
  Si7021: Si7021 humidity and temperature sensor
  BH1750: Light Sensor
